# Fritzing sketch time-glow (saved by Fritzing 0.9.10b)

parts:
  Arduino = Arduino Nano (Rev3.0) (ICSP)
  12_LED_RGB_Ring = 12 NeoPixel Ring [part_number=1643]
  Rotary_Encoder_+_Switch = KY-040 Rotary encoder [package=THT]
  Buzzer = Piezo Speaker
  R1 = Resistor [tolerance=±5% power=0.25 resistance=100 package=THT]

nets:
  N1: Arduino.D3, Rotary_Encoder_+_Switch.DT
  N2: Arduino.D4, Rotary_Encoder_+_Switch.CLK
  N3: Arduino.D5, Rotary_Encoder_+_Switch.SW
  N4: Arduino.D6, Buzzer.pin2
  N5: Arduino.D7, 12_LED_RGB_Ring.IN
  GND: Arduino.GND, 12_LED_RGB_Ring.GND, Rotary_Encoder_+_Switch.GND, R1.Pin_1
  5V: Arduino.5V, 12_LED_RGB_Ring.VDD, Rotary_Encoder_+_Switch.Vcc
  N6: Buzzer.pin1, R1.Pin_0

custom parts:
  12 NeoPixel Ring: 12 ultra bright smart LED NeoPixels are arranged in a circle with 1.5" (37mm) outer diameter. The rings are 'chainable' - connect the output pin of one to the input pin of another. Use only one microcontroller pin to control as many as you can chain together! Each LED is addressable as the driver chip is inside the LED. Each one has ~18mA constant current drive so the color will be very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
  KY-040 Rotary encoder: KY-040 Rotary Encoder with switch on breakout borad from AZ Delivery

// code stored in the sketch: Untitled.ino
#include <Arduino.h>
#include <Encoder.h>
#include <FastLED.h>
#include <LowPower.h>

// Rotary Encoder Pins
#define ENCODER_PIN_A 2
#define ENCODER_PIN_B 3
#define ENCODER_BTN_PIN 4

// RGB LED Ring Pins
#define LED_PIN 5
#define NUM_LEDS 12
#define BRIGHTNESS 255

// Buzzer Pin
#define BUZZER_PIN 6

// LED Colors
const CRGB colors[] = {CRGB::Blue, CRGB::Red, CRGB::Green, CRGB::Purple, CRGB::Orange};

CRGB leds[NUM_LEDS];
Encoder myEncoder(ENCODER_PIN_A, ENCODER_PIN_B);
volatile bool encoderChanged = false;
volatile bool buttonPressed = false;
uint8_t selectedColorIndex = 0;
uint8_t selectedDuration = 0;

void setup() {
  FastLED.addLeds<WS2812B, LED_PIN, GRB>(leds, NUM_LEDS);
  FastLED.setBrightness(BRIGHTNESS);

  pinMode(ENCODER_BTN_PIN, INPUT_PULLUP);
  pinMode(BUZZER_PIN, OUTPUT);
  digitalWrite(BUZZER_PIN, LOW);

  attachInterrupt(digitalPinToInterrupt(ENCODER_PIN_A), encoderInterrupt, CHANGE);
  attachInterrupt(digitalPinToInterrupt(ENCODER_PIN_B), encoderInterrupt, CHANGE);
  attachInterrupt(digitalPinToInterrupt(ENCODER_BTN_PIN), buttonInterrupt, FALLING);
}

void loop() {
  if (encoderChanged) {
    encoderChanged = false;
    selectedDuration = (selectedDuration + 5) % 65;
    displayDuration(selectedDuration);
  }

  if (buttonPressed) {
    buttonPressed = false;

    if (selectedColorIndex < 4) {
      selectedColorIndex++;
    } else {
      selectedColorIndex = 0;
      countdown(selectedDuration);
      beep(5);
      selectedDuration = 0;
      LowPower.powerDown(SLEEP_FOREVER, ADC_OFF, BOD_OFF);
    }

    displayColor(selectedColorIndex);
  }
}

void encoderInterrupt() {
  encoderChanged = true;
}

void buttonInterrupt() {
  buttonPressed = true;
}

void displayDuration(uint8_t minutes) {
  uint8_t ledCount = map(minutes, 0, 60, 0, 12);

  for (uint8_t i = 0; i < NUM_LEDS; i++) {
    if (i < ledCount) {
      leds[i] = colors[selectedColorIndex];
    } else {
      leds[i] = CRGB::Black;
    }
  }

  FastLED.show();
}

void displayColor(uint8_t colorIndex) {
  for (uint8_t i = 0; i < NUM_LEDS; i++) {
    leds[i] = colors[colorIndex];
  }

  FastLED.show();
}

void countdown(uint8_t minutes) {
  uint32_t interval = 1000;
  uint32_t endTime = millis() + minutes * 60 * 1000;
  uint8_t fadeDirection = 1;

  while (millis() < endTime) {
    FastLED.setBrightness(BRIGHTNESS * fadeDirection);
    FastLED.show();

    delay(interval);

    fadeDirection = (fadeDirection == 1) ? 0 : 1;
  }
}

void beep(uint8_t seconds) {
  uint32_t interval = 500;
  uint32_t endTime = millis() + seconds * 1000;
